# Fritzing sketch EPS32Car (saved by Fritzing 1.0.3b)
breadboards: 3

parts:
  M1 = ESP32-S2-DevKitC-1 [part_number=ESP32-S2-DevKitC-1]
  R1 = Photocell (LDR) [power=0.25W dark_resistance_@0.01lx=300kΩ light_resistance_@100lx=400Ω luminance=10lx package=THT]
  R2 = Resistor [tolerance=±5% resistance=220 package="0805 [SMD]"]
  SW2 = DIP Switch 8 Position [package=dipswitch-08]
  R3 = Resistor [tolerance=±5% resistance=220 package="0805 [SMD]"]
  R4 = Resistor [tolerance=±5% resistance=220 package="0805 [SMD]"]
  R5 = Resistor [tolerance=±5% resistance=220 package="0805 [SMD]"]
  R6 = Resistor [tolerance=±5% resistance=220 package="0805 [SMD]"]
  R7 = Resistor [tolerance=±5% resistance=220 package="0805 [SMD]"]
  LED1 = smd LED [color="Red (633nm)" package="0603 [SMD]"]
  LED2 = smd LED [color="Orange (620nm)" package="0603 [SMD]"]
  IC1 = L293D [package=THT]
  M2 = DC Motor [voltage_(max)=6V voltage_(min)=3V]
  R8 = Rotary Potentiometer (Small) [maximum_resistance=10kΩ knob_status=50% power=0.5W package=THT]
  LED3 = smd LED [color="Red (633nm)" package="0603 [SMD]"]  # not connected
  LED4 = smd LED [color="Blue (470nm)" package="0603 [SMD]"]
  LED5 = smd LED [color="Yellow (595nm)" package="0603 [SMD]"]
  R9 = Resistor [tolerance=±5% resistance=220 package="0805 [SMD]"]
  R10 = Resistor [tolerance=±5% resistance=220 package="0805 [SMD]"]
  S1 = Pushbutton [package="[THT]"]
  S2 = Pushbutton [package="[THT]"]
  J1 = Piezo Speaker
  U1 = A3144 Hall Effect Sensor. [package="UA [THT]"]
  R11 = Resistor [tolerance=±5% resistance=220 package="0805 [SMD]"]

nets:
  N1: M1.pin_1, M1.pin_2
  N2: M1.pin_4, IC1.Enable_1
  N3: M1.pin_5, IC1.In_1
  N4: M1.pin_6, IC1.In_2
  N5: M1.pin_7, S2.Pin_1, S2.Pin_2
  N6: M1.pin_8, S1.Pin_1, S1.Pin_2
  N7: M1.pin_9, J1.pin2
  N8: M1.pin_10, U1.+Vsupply, R11.Pin_0
  N9: M1.pin_15, R8.wiper
  N10: M1.pin_21, IC1.+Vmotor, IC1.+V, R8.leg2, U1.Out, R11.Pin_1
  N11: M1.pin_22, M1.pin_23, M1.pin_24, M1.pin_44, R2.Pin_0
  N12: M1.pin_25, LED1.anode
  N13: M1.pin_27, LED2.anode
  N14: M1.pin_29, LED4.anode
  N15: M1.pin_31, LED5.anode
  N16: M1.pin_34, SW2.8
  N17: M1.pin_35, SW2.7
  N18: M1.pin_36, M1.pin_37, SW2.4
  N19: M1.pin_38, SW2.3
  N20: M1.pin_40, R1.pin_0, R2.Pin_1
  N21: SW2.14, R5.Pin_1
  N22: SW2.15, R4.Pin_1
  N23: SW2.16, R3.Pin_1
  N24: R3.Pin_0, R4.Pin_0, R5.Pin_0, R6.Pin_1, R7.Pin_1, IC1.0V, R8.leg1, R9.Pin_1, R10.Pin_1, S1.Pin_3, S1.Pin_4, S2.Pin_3, S2.Pin_4, J1.pin1, U1.GND
  N25: R6.Pin_0, LED1.cathode
  N26: R7.Pin_0, LED2.cathode
  N27: IC1.Out_1_(_Controlled_by_Enable_1_), M2.pin_1
  N28: IC1.Out_2_(_Controlled_by_Enable_1_), M2.pin_2
  N29: LED4.cathode, R9.Pin_0
  N30: LED5.cathode, R10.Pin_0

custom parts:
  ESP32-S2-DevKitC-1: ESP32-S2-DevKitC-1 is an entry-level development board based on ESP32-S2-SOLO (on-board PCB antenna). It is based on the ESP32 microcontroller that boasts Wifi, Bluetooth, Ethernet and Low Power support all in a single chip. (vanepp) Feb 2022: converted to ESP32-S2-DevKitC-1. This module is 44pins long (2x22) and 11 pins width.
  A3144 Hall Effect Sensor.: Allegro A3144 hall effect switch for high temperature operation.
